# Fritzing sketch Bluetooth-Car (saved by Fritzing 0.9.3b)

parts:
  S1 = H-Bridge with L298N
  Часть1 = Arduino Uno (Rev3)
  M1 = DC Motor
  M2 = DC Motor
  M3 = DC Motor
  M4 = DC Motor
  J1 = Basic Servo
  J2 = Basic Servo
  BAT1 = BC9VPC [package=bc9vpc]
  BAT2 = BC9VPC [package=bc9vpc]

nets:
  N1: S1.12V, BAT1.V+, BAT2.V+
  N2: S1.GND, BAT1.V-, BAT2.V-
  N3: S1.ENA, Часть1.D6_PWM
  N4: S1.IN1, Часть1.D4
  N5: S1.IN2, Часть1.D3_PWM
  N6: S1.IN3, Часть1.D8
  N7: S1.IN4, Часть1.D7
  N8: S1.ENB, Часть1.D5_PWM
  N9: S1.M1-01, M3.pin_2, M4.pin_2
  N10: S1.M1-02, M3.pin_1, M4.pin_1
  N11: S1.M2-01, M1.pin_2, M2.pin_2
  N12: S1.M2-02, M1.pin_1, M2.pin_1
  N13: Часть1.A0, J2.pulse
  N14: Часть1.A1, J1.pulse
  VCC: Часть1.5V, J1.vcc, J2.vcc
  GND: Часть1.GND, J1.gnd, J2.gnd

custom parts:
  H-Bridge with L298N: h-bridge
